// Logisim project DDCA PPT.circ as structural Verilog: 1 circuit, main circuit main
module main (
  input  [3:0] in_1,
  input  [3:0] in_2,
  input  [3:0] in_3,
  input  [3:0] in_4,
  input  [3:0] in_5,
  input  [3:0] NOT_gate,
  input  [3:0] in_7,
  output [3:0] out_8,
  output [3:0] out_9
);

  wire comparator_1_eq, comparator_1_lt;
  wire [3:0] adder_1_out, adder_3_out, undriven, undriven_2;

  Adder #(.width(4)) adder_1 (.a(in_5), .b(in_7), .out(adder_1_out), .cin(1'b0));  // open: cout
  assign out_9 = ~NOT_gate;  // NOT_Gate not_1, 4 bits wide
  Adder #(.width(4)) adder_2 (.a(in_1), .b(in_3), .out(out_8), .cin(1'b0));  // open: cout
  Adder #(.width(4)) adder_3 (.a(undriven_2), .b(undriven), .out(adder_3_out), .cin(1'b0));  // open: cout
  LED led_1 (.in(comparator_1_eq));
  Comparator #(.width(4)) comparator_1 (.a(in_2), .b(in_4), .eq(comparator_1_eq), .lt(comparator_1_lt));  // open: gt
  LED led_2 (.in(comparator_1_lt));

  // Notes on the sheet:
  //   adder
  //   Adder
  //   Adder
  //   comparator
endmodule
